# Fritzing sketch master fritzing (saved by Fritzing 0.9.3b)
breadboards: 1

parts:
  Componente1 = Arduino Uno (Rev3)
  Componente2 = NRF24L01+ Breakout Board
  S1 = Pushbutton [package="[SMD]"]

nets:
  N1: Componente1.D9_PWM, Componente2.CE
  N2: Componente1.D10_PWM/SS, Componente2.CS
  N3: Componente1.D11_PWM/MOSI, Componente2.MOSI
  N4: Componente1.D12/MISO, Componente2.MISO
  N5: Componente1.D13/SCK, Componente2.SCK
  N6: Componente1.D2, S1.Pin_3, S1.Pin_4
  3V3: Componente1.3V3, Componente2.VCC
  GND: Componente1.GND, Componente2.GND, S1.Pin_1, S1.Pin_2
