# Fritzing sketch slave fritzing (saved by Fritzing 0.9.3b)
breadboards: 1

parts:
  Componente1 = NRF24L01+ Breakout Board
  Componente2 = Arduino Uno (Rev3)
  LED1 = smd LED [color="Red (633nm)" package="0603 [SMD]"]
  R1 = Resistor [tolerance=±5% resistance=220 package="0603 [SMD]"]

nets:
  GND: Componente1.GND, Componente2.GND, LED1.cathode
  VCC: Componente1.VCC, Componente2.3V3
  N1: Componente1.CE, Componente2.D9_PWM
  N2: Componente1.CS, Componente2.D10_PWM/SS
  N3: Componente1.SCK, Componente2.D13/SCK
  N4: Componente1.MOSI, Componente2.D11_PWM/MOSI
  N5: Componente1.MISO, Componente2.D12/MISO
  N6: Componente2.D3_PWM, R1.Pin_1
  N7: LED1.anode, R1.Pin_0
